// Logisim project sequenceDetector.circ as structural Verilog
module main (
  input  clk,
  input  reset,
  input  x,
  output [2:0] Q
);

  wire seq_detector_moore_1_z;

  LED led_1 (.in(clk));
  LED led_2 (.in(reset));
  LED led_3 (.in(x));
  LED z (.in(seq_detector_moore_1_z));
  seq_detector_moore seq_detector_moore_1 (.clk(clk), .reset(reset), .x(x), .z(seq_detector_moore_1_z), .Q(Q));
endmodule

// VHDL entity seq_detector_moore, as the project stores it:
library ieee;
use ieee.std_logic_1164.all;

entity seq_detector_moore is
  port (
    clk   : in  std_logic;
    reset : in  std_logic;                   -- synchronous, active-high
    x     : in  std_logic;                   -- serial bit
    z     : out std_logic;                   -- 1-cycle pulse on 001/010/110
    Q     : out std_logic_vector(2 downto 0) -- state to LEDs (debug)
  );
end seq_detector_moore;

architecture rtl of seq_detector_moore is
  type state_t is (START, S0, S1, S00, S01, S10, S11, DETECT);
  signal current_state : state_t := START;
  signal next_state    : state_t := START;
begin
  -- State register (synchronous reset)
  state_reg : process(clk)
  begin
    if rising_edge(clk) then
      if reset = '1' then
        current_state <= START;
      else
        current_state <= next_state;
      end if;
    end if;
  end process;

  -- Next-state logic (combinational)
  next_logic : process(current_state, x)
  begin
    next_state <= current_state;  -- default hold
    case current_state is
      when START =>
        if x='0' then next_state <= S0  else next_state <= S1  end if;

      when S0 =>
        if x='0' then next_state <= S00 else next_state <= S01 end if;

      when S1 =>
        if x='0' then next_state <= S10 else next_state <= S11 end if;

      -- detect 001
      when S00 =>
        if x='1' then next_state <= DETECT else next_state <= S00 end if;

      -- detect 010
      when S01 =>
        if x='0' then next_state <= DETECT else next_state <= S11 end if;

      when S10 =>
        if x='0' then next_state <= S00 else next_state <= S01 end if;

      -- detect 110
      when S11 =>
        if x='0' then next_state <= DETECT else next_state <= S11 end if;

      -- non-overlap: consume and restart
      when DETECT =>
        next_state <= START;
    end case;
  end process;

  -- Moore output (1 exactly in DETECT)
  z <= '1' when current_state = DETECT else '0';

  -- Export a code to LEDs for debugging (arbitrary encoding)
  with current_state select
    Q <= "000" when START,
         "001" when S0,
         "010" when S1,
         "011" when S00,
         "100" when S01,
         "101" when S10,
         "110" when S11,
         "111" when DETECT;
end rtl;
